# Fritzing sketch Schematic-v2 (saved by Fritzing 0.9.3b)

parts:
  Bauteil3 = Adafruit BME280
  Bauteil4 = Adafruit TSL2561 [part_number="Adafruit #439"]
  Bauteil5 = VEML6070 [part_number=VEML6070]
  LED1 = smd LED [color="Red (635nm)" package="0603 [SMD]"]
  R2 = Resistor [tolerance=±5% resistance=100 package="2512 [SMD]"]
  P82B715 = IC, DIP package, 8 pins [chip_label=P82B715]
  SCL = Header 1 [package=snap-female]
  SDA = Header 1 [package=snap-female]
  R5 = Resistor [tolerance=±5% resistance=68 package="0603 [SMD]"]
  R6 = Resistor [tolerance=±5% resistance=68 package="0603 [SMD]"]
  VCC = Header 1 [package=snap-female]
  GND' = Header 1 [package=snap-female]
  P82B716 = IC, DIP package, 8 pins [chip_label=P82B715]
  IRLZ44N = Basic FET N-Channel [package="TO220 [THT]"]
  R3 = Resistor [tolerance=±5% resistance=100 package="2512 [SMD]"]
  R4 = Resistor [tolerance=±5% resistance=1M package="2512 [SMD]"]
  P82B717 = IC, DIP package, 8 pins [chip_label=P82B715]
  R8 = Resistor [tolerance=±5% resistance=68 package="0603 [SMD]"]
  R7 = Resistor [tolerance=±5% resistance=68 package="0603 [SMD]"]
  R9 = Resistor [tolerance=±5% resistance=4.7k package="0603 [SMD]"]
  V1 = DC Power [voltage=5]
  S1 = SWITCH-MOMENTARY-2 [package=tactile-switch-1101ne]
  ZS-042_RTC2 = ZS-042 RTC Module
  NJU7223 = V_REG_LD1117VXX [package=78xxl]
  C1 = Tantalum Capacitor [capacitance=100nF package="C 6032 [SMD, tantalum]"]
  C2 = Tantalum Capacitor [capacitance=100nF package="C 6032 [SMD, tantalum]"]
  S2 = SWITCH-MOMENTARY-2 [package=tactile-switch-1101ne]
  GND = Header 1 [package=snap-female]
  WeMos_D1_Mini1 = WeMos D1 Mini
  EN = Header 1 [package=snap-female]
  VCC_2 = Header 1 [package=snap-female]
  GND_2 = Header 1 [package=snap-female]
  1-Wire = Header 1 [package=snap-female]
  3V3 = Header 1 [package=snap-female]
  R10 = Resistor [tolerance=±5% resistance=4.7k package="0603 [SMD]"]
  R11 = Resistor [tolerance=±5% resistance=4.7k package="0603 [SMD]"]
  R12 = Resistor [tolerance=±5% resistance=4.7k package="0603 [SMD]"]
  R13 = Resistor [tolerance=±5% resistance=4.7k package="0603 [SMD]"]
  GND_3 = Header 1 [package=snap-female]
  DS2 = DS18B20 1-Wire Temperature Sensor [part_number=DS18B20]
  R14 = Resistor [tolerance=±5% resistance=4.7k package="0603 [SMD]"]
  R15 = Resistor [tolerance=±5% resistance=4.7k package="0603 [SMD]"]
  D1 = Schottky Diode [part_number=BAT42 package="300 mil [THT]"]

nets:
  VIN: Bauteil3.VIN, Bauteil4.VIN, Bauteil5.VDD, R2.Pin_0, P82B715.pin8, R5.Pin_1, R6.Pin_1, VCC.1, P82B716.pin8, P82B717.pin8, R8.Pin_1, R7.Pin_1, R9.Pin_1, ZS-042_RTC2.VCC, NJU7223.OUT, C2.+, WeMos_D1_Mini1.3V3, VCC_2.1, 3V3.1, R10.Pin_0, R11.Pin_0, R12.Pin_0, R13.Pin_0, DS2.VDD
  GND: Bauteil3.GND, Bauteil4.GND, Bauteil5.GND, P82B715.pin4, GND'.1, P82B716.pin4, IRLZ44N.drain, P82B717.pin4
  N1: Bauteil3.SCK/SCL, P82B716.pin6, R11.Pin_1
  N2: Bauteil3.SDI/SDA, P82B716.pin3, R10.Pin_1
  N3: Bauteil4.SDA, Bauteil5.SDA, P82B717.pin3, R12.Pin_1
  N4: Bauteil4.SCL, Bauteil5.SCL, P82B717.pin6, R13.Pin_1
  N5: LED1.cathode, WeMos_D1_Mini1.D4
  N6: LED1.anode, R2.Pin_1
  N7: P82B715.pin2, R5.Pin_0, P82B716.pin2, P82B717.pin2, R7.Pin_0
  N8: P82B715.pin3, SDA.1, ZS-042_RTC2.SDA, WeMos_D1_Mini1.D2, R15.Pin_0
  N9: P82B715.pin6, SCL.1, ZS-042_RTC2.SCL, WeMos_D1_Mini1.D1, R14.Pin_1
  N10: P82B715.pin7, R6.Pin_0, P82B716.pin7, P82B717.pin7, R8.Pin_0
  N11: IRLZ44N.gate, R3.Pin_1, R4.Pin_0
  GND_2: IRLZ44N.source, R4.Pin_1, V1.V-, ZS-042_RTC2.GND, NJU7223.GND, C1.-, C2.-, GND.1, WeMos_D1_Mini1.G, GND_2.1, GND_3.1, DS2.GND
  N12: R3.Pin_0, WeMos_D1_Mini1.D7, EN.1
  N13: R9.Pin_0, WeMos_D1_Mini1.D6, 1-Wire.1, DS2.DQ
  N14: V1.V+, S1.2
  N15: S1.1, NJU7223.IN, C1.+
  N16: S2.1, D1.anode
  N17: S2.2, WeMos_D1_Mini1.RST
  N18: WeMos_D1_Mini1.D0, D1.cathode
  N19: R14.Pin_0, R15.Pin_1

custom parts:
  Adafruit BME280: Bosch has stepped up their game with their new BME280 sensor, an environmental sensor with temperature, barometric pressure and humidity! This sensor is great for all sorts of weather/environmental sensing and can even be used in both I2C and SPI! This precision sensor from Bosch is the best low-cost sensing solution for measuring humidity with ±3% accuracy, barometric pressure with ±1 hPa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
  Adafruit TSL2561: The TSL2561 luminosity sensor is an advanced digital light sensor, ideal for use in a wide range of light situations. Compared to low cost CdS cells, this sensor is more precise, allowing for exact lux calculations and can be configured for different gain/timing ranges to detect light ranges from up to 0.1 - 40,000+ Lux on the fly. The best part of this sensor is that it contains both infrared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
  VEML6070: This little sensor is a great way to add UV light sensing to any microcontroller project. The VEML6070 from Vishay has a true UV A light sensor and an I2C-controlled ADC that will take readings and integrate them for you over ~60ms to 500ms.
  ZS-042 RTC Module: This is the ZS-042 RTC module which uses the Maxim DS3231 real time clock IC. The module has a battery holder for a LIR2032 or CR2032. The module also includes an Atmel AT24C32 32K EEPROM for storing important information. The module can operate at 3V3 and 5V.
